// Logisim project sqrt2.circ as structural Verilog: 44 circuits, main circuit main
module main (
  input  ENABLE,
  input  [15:0] IO_DATA_IN,
  output NAN,
  output PINF,
  output NINF,
  output RESULT,
  output [15:0] IO_DATA_OUT
);

  wire CLK_out;

  Clock CLK (.out(CLK_out));
  sqrt sqrt_1 (
    .CLK(CLK_out), .ENABLE(ENABLE), .IO_DATA_IN(IO_DATA_IN), .IS_NAN(NAN), .IS_PINF(PINF), .IS_NINF(NINF),
    .RESULT(RESULT), .IO_DATA_OUT(IO_DATA_OUT));
endmodule

module sqrt (
  input  CLK,
  input  ENABLE,
  input  [15:0] IO_DATA_IN,
  output IS_NAN,
  output IS_PINF,
  output IS_NINF,
  output RESULT,
  output [15:0] IO_DATA_OUT
);

  wire and_2_out, and_3_out, and_5_out, CLK_t, comparator_24bit_1_a_equal_b, comparator_24bit_1_a_smaller_b,
       comparator_24bit_2_a_smaller_b, comparator_24bit_3_a_bigger_b, comparator_24bit_3_a_equal_b,
       comparator_24bit_3_a_smaller_b, from_24_1_1_io_data, get_info_1_sign, GREATER_THAN_FIRST_TACT,
       IS_12_TACT, IS_FIRST_TACT, nand_1_out, NCLK, new_rem_borrow_out, not_1_out, not_3_out, not_4_out,
       not_5_out, not_8_out, not_9_out, not_10_out, not_11_out, or_1_out, or_4_out,
       res_plus_shift_1_borrow_out, special, summator_24bit_1_borrow_out, transmission_1_p3,
       transmission_2_p4;
  wire [3:0] counter_4bit_1_out_3, special_cases_1_nan;
  wire [4:0] from_24_5_1_io_data, get_info_1_exp;
  wire [9:0] from_24_10_1_io_data, get_info_1_mantissa;
  wire [10:0] from_10_11_1_io_data;
  wire [15:0] from_24_16_1_io_in, get_res_1_res, transmission_2_p2;
  wire [23:0] correct_exp_and_mant_1_new_exp, correct_exp_and_mant_1_new_mant, exp, from_1_24_1_out_2,
       from_2_24_1_io_out, from_4_24_1_io_in, from_4_24_2_io_in, from_5_24_1_io_in, from_10_24_1_io_in,
       from_16_24_1_io_data, if_expression_1_io_out, if_expression_2_io_out, if_expression_3_io_out,
       if_expression_4_io_out, mant, memory_cell_24bit_1_data_out, memory_cell_24bit_2_data_out,
       new_rem_io_out, old_exp_data_out, old_mant_data_out, out_special_case, read_dem, read_rem, read_res,
       res_plus_shift_1_io_out, shift_left_1_io_out, shift_left_2_io_out, shift_left_3_io_out,
       shift_left_5_io_out, shift_left_6_io_out, sign, substructor_24bit_1_out_3, summator_24bit_1_io_out,
       write_dem, Write_demolished_data_out, write_rem, Write_remainder_data_out, write_res,
       Write_result_data_out;

  not not_1 (not_1_out, CLK);
  and and_1 (CLK_t, ~IS_12_TACT, not_1_out);  // AND_Gate
  comparator_24bit comparator_24bit_1 (
    .B(from_4_24_1_io_in), .A(24'hc), .A_smaller_B(comparator_24bit_1_a_smaller_b),
    .A_equal_B(comparator_24bit_1_a_equal_b));  // open: A_bigger_B
  get_res get_res_1 (.mant(read_res), .exp(exp), .sign(sign), .res(get_res_1_res));
  not not_2 (NCLK, CLK_t);
  from_4_24 from_4_24_1 (.IO_DATA(counter_4bit_1_out_3), .IO_IN(from_4_24_1_io_in));
  or or_1 (or_1_out, comparator_24bit_1_a_smaller_b, comparator_24bit_1_a_equal_b);
  not not_3 (not_3_out, ENABLE);
  counter_4bit counter_4bit_1 (.C(not_1_out), .ENABLE(ENABLE), .out_3(counter_4bit_1_out_3));
  memory_cell_24bit memory_cell_24bit_1 (
    .IO_DATA_IN(if_expression_1_io_out), .C(NCLK), .ENABLE(ENABLE), .DATA_OUT(memory_cell_24bit_1_data_out));
  if_expression if_expression_1 (
    .A(out_special_case), .expression(special), .B(from_16_24_1_io_data), .IO_OUT(if_expression_1_io_out));
  from_16_24 from_16_24_1 (.IO_IN(get_res_1_res), .IO_DATA(from_16_24_1_io_data));
  d_trigger d_trigger_1 (.C(or_1_out), .D(1'b1), .ENABLE(not_3_out), .Q(IS_12_TACT));  // open: NQ
  and and_2 (and_2_out, ~counter_4bit_1_out_3[0], ~counter_4bit_1_out_3[1], ~counter_4bit_1_out_3[2], ~counter_4bit_1_out_3[3]);  // AND_Gate
  not not_4 (not_4_out, comparator_24bit_2_a_smaller_b);
  comparator_24bit comparator_24bit_2 (
    .B(from_4_24_1_io_in), .A(24'h1), .A_smaller_B(comparator_24bit_2_a_smaller_b));  // open: A_equal_B, A_bigger_B
  and and_3 (and_3_out, CLK_t, not_5_out);
  not not_5 (not_5_out, nand_1_out);
  nand nand_1 (nand_1_out, and_2_out, ENABLE);
  and and_4 (GREATER_THAN_FIRST_TACT, ~IS_12_TACT, not_4_out);  // AND_Gate
  from_24_16 from_24_16_1 (.IO_DATA(memory_cell_24bit_1_data_out), .IO_IN(from_24_16_1_io_in));
  // Transmission_Gate #(.width(16)) transmission_1: pin names not known; wires that end beside it: from_24_16_1_io_in, GREATER_THAN_FIRST_TACT, transmission_1_p3, IO_DATA_IN
  not not_6 (transmission_1_p3, GREATER_THAN_FIRST_TACT);
  // Transmission_Gate #(.width(16)) transmission_2: pin names not known; wires that end beside it: IS_FIRST_TACT, transmission_2_p2, IO_DATA_IN, transmission_2_p4
  not not_7 (transmission_2_p4, IS_FIRST_TACT);
  not not_8 (not_8_out, ENABLE);
  get_info get_info_1 (
    .IO_IN(transmission_2_p2), .mantissa(get_info_1_mantissa), .exp(get_info_1_exp), .sign(get_info_1_sign));
  from_10_11 from_10_11_1 (.IO_IN(get_info_1_mantissa), .IO_DATA(from_10_11_1_io_data));
  d_trigger d_trigger_2 (.C(counter_4bit_1_out_3[0]), .D(1'b1), .ENABLE(not_8_out), .Q(IS_FIRST_TACT));  // open: NQ
  from_1_24 from_1_24_1 (.IO_IN(get_info_1_sign), .out_2(from_1_24_1_out_2));
  correct_exp_and_mant correct_exp_and_mant_1 (
    .exp(get_info_1_exp), .mantissa(from_10_11_1_io_data), .new_exp(correct_exp_and_mant_1_new_exp),
    .new_mant(correct_exp_and_mant_1_new_mant));
  not not_9 (not_9_out, IS_FIRST_TACT);
  not not_10 (not_10_out, IS_FIRST_TACT);
  not not_11 (not_11_out, IS_FIRST_TACT);
  special_cases special_cases_1 (
    .mant(get_info_1_mantissa), .exp(get_info_1_exp), .sign(get_info_1_sign), .NAN(special_cases_1_nan[0]),
    .PINF(special_cases_1_nan[1]), .NINF(special_cases_1_nan[2]), .ZERO(special_cases_1_nan[3]));
  from_5_24 from_5_24_1 (.IO_DATA(get_info_1_exp), .IO_IN(from_5_24_1_io_in));
  memory_cell_24bit u_sign (.IO_DATA_IN(from_1_24_1_out_2), .C(and_3_out), .ENABLE(ENABLE), .DATA_OUT(sign));
  memory_cell_24bit new_exp (
    .IO_DATA_IN(correct_exp_and_mant_1_new_exp), .C(and_3_out), .ENABLE(ENABLE), .DATA_OUT(exp));
  memory_cell_24bit new_mant (
    .IO_DATA_IN(correct_exp_and_mant_1_new_mant), .C(and_3_out), .ENABLE(ENABLE), .DATA_OUT(mant));
  if_expression if_expression_2 (
    .A(mant), .expression(not_9_out), .B(Write_demolished_data_out), .IO_OUT(if_expression_2_io_out));
  if_expression if_expression_3 (
    .A({24{1'b0}}), .expression(not_10_out), .B(Write_remainder_data_out), .IO_OUT(if_expression_3_io_out));
  if_expression if_expression_4 (
    .A({24{1'b0}}), .expression(not_11_out), .B(Write_result_data_out), .IO_OUT(if_expression_4_io_out));
  // Probe on sign
  // Probe on exp
  // Probe on mant
  memory_cell_24bit Read_demolished (
    .IO_DATA_IN(if_expression_2_io_out), .C(CLK_t), .ENABLE(ENABLE), .DATA_OUT(read_dem));
  // Probe on Write_demolished_data_out
  memory_cell_24bit Write_demolished (
    .IO_DATA_IN(write_dem), .C(NCLK), .ENABLE(ENABLE), .DATA_OUT(Write_demolished_data_out));
  memory_cell_24bit Read_remainder (
    .IO_DATA_IN(if_expression_3_io_out), .C(CLK_t), .ENABLE(ENABLE), .DATA_OUT(read_rem));
  // Probe on Write_remainder_data_out
  memory_cell_24bit Write_remainder (
    .IO_DATA_IN(write_rem), .C(NCLK), .ENABLE(ENABLE), .DATA_OUT(Write_remainder_data_out));
  memory_cell_24bit Read_result (.IO_DATA_IN(if_expression_4_io_out), .C(CLK_t), .ENABLE(ENABLE), .DATA_OUT(read_res));
  // Probe on Write_result_data_out
  memory_cell_24bit Write_result (.IO_DATA_IN(write_res), .C(NCLK), .ENABLE(ENABLE), .DATA_OUT(Write_result_data_out));
  // Probe on read_dem
  // Probe on read_rem
  // Probe on read_res
  from_10_24 from_10_24_1 (.IO_DATA(get_info_1_mantissa), .IO_IN(from_10_24_1_io_in));
  from_4_24 from_4_24_2 (.IO_DATA(special_cases_1_nan), .IO_IN(from_4_24_2_io_in));
  // Probe on read_dem
  // Probe on read_res
  memory_cell_24bit memory_cell_24bit_2 (
    .IO_DATA_IN(from_4_24_2_io_in), .C(and_3_out), .ENABLE(ENABLE), .DATA_OUT(memory_cell_24bit_2_data_out));
  // Probe on old_mant_data_out
  memory_cell_24bit old_mant (
    .IO_DATA_IN(from_10_24_1_io_in), .C(and_3_out), .ENABLE(ENABLE), .DATA_OUT(old_mant_data_out));
  // Probe on old_exp_data_out
  memory_cell_24bit old_exp (
    .IO_DATA_IN(from_5_24_1_io_in), .C(and_3_out), .ENABLE(ENABLE), .DATA_OUT(old_exp_data_out));
  // Probe on read_rem
  shift_left shift_left_1 (.IO_IN(read_dem), .IO_OUT(shift_left_1_io_out));
  shift_left shift_left_2 (.IO_IN(read_res), .IO_OUT(shift_left_2_io_out));
  from_24_5 from_24_5_1 (.IO_IN(old_exp_data_out), .IO_DATA(from_24_5_1_io_data));
  from_2_24 from_2_24_1 (.IO_IN(read_dem[11:10]), .IO_OUT(from_2_24_1_io_out));
  shift_left shift_left_3 (.IO_IN(read_rem), .IO_OUT(shift_left_3_io_out));
  from_24_10 from_24_10_1 (.IO_IN(old_mant_data_out), .IO_DATA(from_24_10_1_io_data));
  from_24_1 from_24_1_1 (.IO_IN(sign), .IO_DATA(from_24_1_1_io_data));
  summator_24bit summator_24bit_1 (
    .A(shift_left_2_io_out), .Borrow_in(1'b0), .B(24'h1), .IO_OUT(summator_24bit_1_io_out),
    .Borrow_out(summator_24bit_1_borrow_out));
  // NoConnect on summator_24bit_1_borrow_out
  shift_left shift_left_4 (.IO_IN(shift_left_1_io_out), .IO_OUT(write_dem));
  shift_left shift_left_5 (.IO_IN(shift_left_3_io_out), .IO_OUT(shift_left_5_io_out));
  shift_left shift_left_6 (.IO_IN(shift_left_2_io_out), .IO_OUT(shift_left_6_io_out));
  or or_2 (special, memory_cell_24bit_2_data_out[0], memory_cell_24bit_2_data_out[1], memory_cell_24bit_2_data_out[2], memory_cell_24bit_2_data_out[3]);
  and and_5 (and_5_out, special, ~GREATER_THAN_FIRST_TACT);  // AND_Gate
  output_special_cases output_special_cases_1 (
    .mant(from_24_10_1_io_data), .exp(from_24_5_1_io_data), .sign(from_24_1_1_io_data),
    .IO_OUT(out_special_case));
  // Probe on write_dem
  or or_3 (RESULT, and_5_out, IS_12_TACT);
  summator_24bit new_rem (
    .A(from_2_24_1_io_out), .Borrow_in(1'b0), .B(shift_left_5_io_out), .IO_OUT(new_rem_io_out),
    .Borrow_out(new_rem_borrow_out));
  // NoConnect on new_rem_borrow_out
  summator_24bit res_plus_shift_1 (
    .A(shift_left_6_io_out), .Borrow_in(1'b0), .B(24'h1), .IO_OUT(res_plus_shift_1_io_out),
    .Borrow_out(res_plus_shift_1_borrow_out));
  // NoConnect on res_plus_shift_1_borrow_out
  and and_6 (IS_NAN, memory_cell_24bit_2_data_out[0], and_5_out);
  and and_7 (IS_PINF, memory_cell_24bit_2_data_out[1], and_5_out);
  and and_8 (IS_NINF, memory_cell_24bit_2_data_out[2], and_5_out);
  comparator_24bit comparator_24bit_3 (
    .B(new_rem_io_out), .A(res_plus_shift_1_io_out), .A_smaller_B(comparator_24bit_3_a_smaller_b),
    .A_equal_B(comparator_24bit_3_a_equal_b), .A_bigger_B(comparator_24bit_3_a_bigger_b));
  or or_4 (or_4_out, comparator_24bit_3_a_smaller_b, comparator_24bit_3_a_equal_b);
  if_expression if_expression_5 (
    .A(summator_24bit_1_io_out), .expression(or_4_out), .B(shift_left_2_io_out), .IO_OUT(write_res));
  // Probe on write_res
  substructor_24bit substructor_24bit_1 (
    .subtrahend(res_plus_shift_1_io_out), .minuend(new_rem_io_out), .out_3(substructor_24bit_1_out_3));
  if_expression if_expression_6 (
    .A(new_rem_io_out), .expression(comparator_24bit_3_a_bigger_b), .B(substructor_24bit_1_out_3),
    .IO_OUT(write_rem));
  // Probe on write_rem

  assign IO_DATA_OUT = IO_DATA_IN;
endmodule

module shift_left (
  input  [23:0] IO_IN,
  output [23:0] IO_OUT
);

  // NoConnect on IO_IN[23]

  assign IO_OUT = {IO_IN[22:0], 1'b0};
endmodule

module substructor (
  input  borrow_in,
  input  minuend,
  input  subtrahend,
  output difference,
  output borrow_out
);

  wire and_1_out, and_2_out, not_1_out, not_2_out, xor_1_out;

  not not_1 (not_1_out, minuend);
  xor xor_1 (xor_1_out, minuend, subtrahend);
  and and_1 (and_1_out, subtrahend, not_1_out);
  not not_2 (not_2_out, xor_1_out);
  and and_2 (and_2_out, not_2_out, borrow_in);
  xor xor_2 (difference, borrow_in, xor_1_out);
  or or_1 (borrow_out, and_2_out, and_1_out);
endmodule

module substructor_24bit (
  input  [23:0] subtrahend,
  input  [23:0] minuend,
  output [23:0] out_3
);

  wire substructor_16bit_1_borrow_out, substructor_16bit_2_borrow_out;
  wire [15:0] bit_extender_1_out, bit_extender_2_out, substructor_16bit_2_difference;

  assign bit_extender_1_out = {{8{1'b0}}, minuend[23:16]};  // Bit_Extender bit_extender_1
  assign bit_extender_2_out = {{8{1'b0}}, subtrahend[23:16]};  // Bit_Extender bit_extender_2
  substructor_16bit substructor_16bit_1 (
    .minuend(minuend[15:0]), .subtrahend(subtrahend[15:0]), .borrow_in(1'b0), .difference(out_3[15:0]),
    .borrow_out(substructor_16bit_1_borrow_out));
  substructor_16bit substructor_16bit_2 (
    .minuend(bit_extender_1_out), .subtrahend(bit_extender_2_out),
    .borrow_in(substructor_16bit_1_borrow_out), .difference(substructor_16bit_2_difference),
    .borrow_out(substructor_16bit_2_borrow_out));
  // NoConnect on substructor_16bit_2_borrow_out
  Bit_Extender #(.in_width(16), .out_width(8), .\type ("zero")) bit_extender_3 (
    .in(substructor_16bit_2_difference), .out(out_3[23:16]));
endmodule

module comparator_1bit (
  input  A,
  input  B,
  input  oldA_smaller_oldB,
  input  oldA_equal_oldB,
  input  oldA_bigger_oldB,
  output A_smaller_B,
  output A_equal_B,
  output A_bigger_B
);

  wire and_1_out, and_2_out, and_3_out, and_5_out, not_1_out, xor_1_out;

  and and_1 (and_1_out, ~A, B);  // AND_Gate
  xor xor_1 (xor_1_out, A, B);
  and and_2 (and_2_out, A, ~B);  // AND_Gate
  not not_1 (not_1_out, xor_1_out);
  and and_3 (and_3_out, oldA_smaller_oldB, not_1_out);
  and and_4 (A_equal_B, not_1_out, oldA_equal_oldB);
  and and_5 (and_5_out, oldA_bigger_oldB, not_1_out);
  or or_1 (A_smaller_B, and_1_out, and_3_out);
  or or_2 (A_bigger_B, and_5_out, and_2_out);
endmodule

module summator_1bit (
  input  A,
  input  B,
  input  borrow_in,
  output Sum,
  output Borrow_out
);

  wire and_1_out, and_2_out, xor_1_out;

  and and_1 (and_1_out, A, B);
  xor xor_1 (xor_1_out, A, B);
  xor xor_2 (Sum, xor_1_out, borrow_in);
  and and_2 (and_2_out, xor_1_out, borrow_in);
  or or_1 (Borrow_out, and_2_out, and_1_out);
endmodule

module summator_4bit (
  input  [3:0] A,
  input  [3:0] B,
  input  Borrow_in,
  output [3:0] IO_OUT,
  output Borrow_out
);

  wire summator_1bit_1_borrow_out, summator_1bit_2_borrow_out, summator_1bit_3_borrow_out;

  summator_1bit summator_1bit_1 (
    .A(A[0]), .B(B[0]), .borrow_in(Borrow_in), .Sum(IO_OUT[0]), .Borrow_out(summator_1bit_1_borrow_out));
  summator_1bit summator_1bit_2 (
    .A(A[1]), .B(B[1]), .borrow_in(summator_1bit_1_borrow_out), .Sum(IO_OUT[1]),
    .Borrow_out(summator_1bit_2_borrow_out));
  summator_1bit summator_1bit_3 (
    .A(A[2]), .B(B[2]), .borrow_in(summator_1bit_2_borrow_out), .Sum(IO_OUT[2]),
    .Borrow_out(summator_1bit_3_borrow_out));
  summator_1bit summator_1bit_4 (
    .A(A[3]), .B(B[3]), .borrow_in(summator_1bit_3_borrow_out), .Sum(IO_OUT[3]), .Borrow_out(Borrow_out));
endmodule

module synch_rs_trigger (
  input  R,
  input  C,
  input  S,
  input  ENABLE,
  output Q,
  output NQ
);

  wire and_1_out, and_2_out, nor_2_out, or_1_out, por_1_out;

  POR por_1 (.out(por_1_out));
  and and_1 (and_1_out, R, C);
  and and_2 (and_2_out, C, S);
  or or_1 (or_1_out, ENABLE, por_1_out);
  nor nor_1 (Q, and_1_out, NQ);
  nor nor_2 (nor_2_out, Q, and_2_out);
  or or_2 (NQ, nor_2_out, or_1_out);
endmodule

module d_trigger (
  input  C,
  input  D,
  input  ENABLE,
  output Q,
  output NQ
);

  wire not_1_out;

  not not_1 (not_1_out, D);
  synch_rs_trigger synch_rs_trigger_1 (.R(not_1_out), .C(C), .S(D), .ENABLE(ENABLE), .Q(Q), .NQ(NQ));
endmodule

module comparator_24bit (
  input  [23:0] B,
  input  [23:0] A,
  output A_smaller_B,
  output A_equal_B,
  output A_bigger_B
);

  wire comparator_16bit_1_a_bigger_b, comparator_16bit_1_a_equal_b, comparator_16bit_1_a_smaller_b;
  wire [15:0] bit_extender_1_out, bit_extender_2_out;

  assign bit_extender_1_out = {{8{1'b0}}, A[23:16]};  // Bit_Extender bit_extender_1
  assign bit_extender_2_out = {{8{1'b0}}, B[23:16]};  // Bit_Extender bit_extender_2
  comparator_16bit comparator_16bit_1 (
    .B(B[15:0]), .A(A[15:0]), .oldA_smaller_B(1'b0), .oldA_equal_B(1'b1), .oldA_bigger_B(1'b0),
    .A_smaller_B(comparator_16bit_1_a_smaller_b), .A_equal_B(comparator_16bit_1_a_equal_b),
    .A_bigger_B(comparator_16bit_1_a_bigger_b));
  comparator_16bit comparator_16bit_2 (
    .B(bit_extender_2_out), .A(bit_extender_1_out), .oldA_smaller_B(comparator_16bit_1_a_smaller_b),
    .oldA_equal_B(comparator_16bit_1_a_equal_b), .oldA_bigger_B(comparator_16bit_1_a_bigger_b),
    .A_smaller_B(A_smaller_B), .A_equal_B(A_equal_B), .A_bigger_B(A_bigger_B));
endmodule

module memory_cell_24bit (
  input  [23:0] IO_DATA_IN,
  input  C,
  input  ENABLE,
  output [23:0] DATA_OUT
);

  wire d_trigger_1_nq, d_trigger_2_nq, d_trigger_3_nq, d_trigger_4_nq, d_trigger_5_nq, d_trigger_6_nq,
       d_trigger_7_nq, d_trigger_8_nq, d_trigger_9_nq, d_trigger_10_nq, d_trigger_11_nq, d_trigger_12_nq,
       d_trigger_13_nq, d_trigger_14_nq, d_trigger_15_nq, d_trigger_16_nq, d_trigger_17_nq, d_trigger_18_nq,
       d_trigger_19_nq, d_trigger_20_nq, d_trigger_21_nq, d_trigger_22_nq, d_trigger_23_nq, d_trigger_24_nq,
       not_1_out;

  not not_1 (not_1_out, ENABLE);
  d_trigger d_trigger_1 (.C(C), .D(IO_DATA_IN[0]), .ENABLE(not_1_out), .Q(DATA_OUT[0]), .NQ(d_trigger_1_nq));
  // NoConnect on d_trigger_1_nq
  d_trigger d_trigger_2 (.C(C), .D(IO_DATA_IN[1]), .ENABLE(not_1_out), .Q(DATA_OUT[1]), .NQ(d_trigger_2_nq));
  // NoConnect on d_trigger_2_nq
  d_trigger d_trigger_3 (.C(C), .D(IO_DATA_IN[2]), .ENABLE(not_1_out), .Q(DATA_OUT[2]), .NQ(d_trigger_3_nq));
  // NoConnect on d_trigger_3_nq
  d_trigger d_trigger_4 (.C(C), .D(IO_DATA_IN[3]), .ENABLE(not_1_out), .Q(DATA_OUT[3]), .NQ(d_trigger_4_nq));
  // NoConnect on d_trigger_4_nq
  d_trigger d_trigger_5 (.C(C), .D(IO_DATA_IN[4]), .ENABLE(not_1_out), .Q(DATA_OUT[4]), .NQ(d_trigger_5_nq));
  // NoConnect on d_trigger_5_nq
  d_trigger d_trigger_6 (.C(C), .D(IO_DATA_IN[5]), .ENABLE(not_1_out), .Q(DATA_OUT[5]), .NQ(d_trigger_6_nq));
  // NoConnect on d_trigger_6_nq
  d_trigger d_trigger_7 (.C(C), .D(IO_DATA_IN[6]), .ENABLE(not_1_out), .Q(DATA_OUT[6]), .NQ(d_trigger_7_nq));
  // NoConnect on d_trigger_7_nq
  d_trigger d_trigger_8 (.C(C), .D(IO_DATA_IN[7]), .ENABLE(not_1_out), .Q(DATA_OUT[7]), .NQ(d_trigger_8_nq));
  // NoConnect on d_trigger_8_nq
  d_trigger d_trigger_9 (.C(C), .D(IO_DATA_IN[8]), .ENABLE(not_1_out), .Q(DATA_OUT[8]), .NQ(d_trigger_9_nq));
  // NoConnect on d_trigger_9_nq
  d_trigger d_trigger_10 (.C(C), .D(IO_DATA_IN[9]), .ENABLE(not_1_out), .Q(DATA_OUT[9]), .NQ(d_trigger_10_nq));
  // NoConnect on d_trigger_10_nq
  d_trigger d_trigger_11 (.C(C), .D(IO_DATA_IN[10]), .ENABLE(not_1_out), .Q(DATA_OUT[10]), .NQ(d_trigger_11_nq));
  // NoConnect on d_trigger_11_nq
  d_trigger d_trigger_12 (.C(C), .D(IO_DATA_IN[11]), .ENABLE(not_1_out), .Q(DATA_OUT[11]), .NQ(d_trigger_12_nq));
  // NoConnect on d_trigger_12_nq
  d_trigger d_trigger_13 (.C(C), .D(IO_DATA_IN[12]), .ENABLE(not_1_out), .Q(DATA_OUT[12]), .NQ(d_trigger_13_nq));
  // NoConnect on d_trigger_13_nq
  d_trigger d_trigger_14 (.C(C), .D(IO_DATA_IN[13]), .ENABLE(not_1_out), .Q(DATA_OUT[13]), .NQ(d_trigger_14_nq));
  // NoConnect on d_trigger_14_nq
  d_trigger d_trigger_15 (.C(C), .D(IO_DATA_IN[14]), .ENABLE(not_1_out), .Q(DATA_OUT[14]), .NQ(d_trigger_15_nq));
  // NoConnect on d_trigger_15_nq
  d_trigger d_trigger_16 (.C(C), .D(IO_DATA_IN[15]), .ENABLE(not_1_out), .Q(DATA_OUT[15]), .NQ(d_trigger_16_nq));
  // NoConnect on d_trigger_16_nq
  d_trigger d_trigger_17 (.C(C), .D(IO_DATA_IN[16]), .ENABLE(not_1_out), .Q(DATA_OUT[16]), .NQ(d_trigger_17_nq));
  // NoConnect on d_trigger_17_nq
  d_trigger d_trigger_18 (.C(C), .D(IO_DATA_IN[17]), .ENABLE(not_1_out), .Q(DATA_OUT[17]), .NQ(d_trigger_18_nq));
  // NoConnect on d_trigger_18_nq
  d_trigger d_trigger_19 (.C(C), .D(IO_DATA_IN[18]), .ENABLE(not_1_out), .Q(DATA_OUT[18]), .NQ(d_trigger_19_nq));
  // NoConnect on d_trigger_19_nq
  d_trigger d_trigger_20 (.C(C), .D(IO_DATA_IN[19]), .ENABLE(not_1_out), .Q(DATA_OUT[19]), .NQ(d_trigger_20_nq));
  // NoConnect on d_trigger_20_nq
  d_trigger d_trigger_21 (.C(C), .D(IO_DATA_IN[20]), .ENABLE(not_1_out), .Q(DATA_OUT[20]), .NQ(d_trigger_21_nq));
  // NoConnect on d_trigger_21_nq
  d_trigger d_trigger_22 (.C(C), .D(IO_DATA_IN[21]), .ENABLE(not_1_out), .Q(DATA_OUT[21]), .NQ(d_trigger_22_nq));
  // NoConnect on d_trigger_22_nq
  d_trigger d_trigger_23 (.C(C), .D(IO_DATA_IN[22]), .ENABLE(not_1_out), .Q(DATA_OUT[22]), .NQ(d_trigger_23_nq));
  // NoConnect on d_trigger_23_nq
  d_trigger d_trigger_24 (.C(C), .D(IO_DATA_IN[23]), .ENABLE(not_1_out), .Q(DATA_OUT[23]), .NQ(d_trigger_24_nq));
  // NoConnect on d_trigger_24_nq
endmodule

module summator_24bit (
  input  [23:0] A,
  input  Borrow_in,
  input  [23:0] B,
  output [23:0] IO_OUT,
  output Borrow_out
);

  wire summator_4bit_1_borrow_out, summator_4bit_2_borrow_out, summator_4bit_3_borrow_out,
       summator_4bit_4_borrow_out, summator_4bit_5_borrow_out;

  summator_4bit summator_4bit_1 (
    .A(A[3:0]), .B(B[3:0]), .Borrow_in(Borrow_in), .IO_OUT(IO_OUT[3:0]),
    .Borrow_out(summator_4bit_1_borrow_out));
  summator_4bit summator_4bit_2 (
    .A(A[7:4]), .B(B[7:4]), .Borrow_in(summator_4bit_1_borrow_out), .IO_OUT(IO_OUT[7:4]),
    .Borrow_out(summator_4bit_2_borrow_out));
  summator_4bit summator_4bit_3 (
    .A(A[11:8]), .B(B[11:8]), .Borrow_in(summator_4bit_2_borrow_out), .IO_OUT(IO_OUT[11:8]),
    .Borrow_out(summator_4bit_3_borrow_out));
  summator_4bit summator_4bit_4 (
    .A(A[15:12]), .B(B[15:12]), .Borrow_in(summator_4bit_3_borrow_out), .IO_OUT(IO_OUT[15:12]),
    .Borrow_out(summator_4bit_4_borrow_out));
  summator_4bit summator_4bit_5 (
    .A(A[19:16]), .B(B[19:16]), .Borrow_in(summator_4bit_4_borrow_out), .IO_OUT(IO_OUT[19:16]),
    .Borrow_out(summator_4bit_5_borrow_out));
  summator_4bit summator_4bit_6 (
    .A(A[23:20]), .B(B[23:20]), .Borrow_in(summator_4bit_5_borrow_out), .IO_OUT(IO_OUT[23:20]),
    .Borrow_out(Borrow_out));
endmodule

module if_expression (
  input  [23:0] A,
  input  expression,
  input  [23:0] B,
  output [23:0] IO_OUT
);

  wire not_1_out, not_2_out;

  not not_1 (not_1_out, expression);
  not not_2 (not_2_out, expression);
  // Transmission_Gate #(.width(24)) transmission_1: pin names not known; wires that end beside it: A, not_1_out, expression, IO_OUT
  // Transmission_Gate #(.width(24)) transmission_2: pin names not known; wires that end beside it: B, not_2_out, expression, IO_OUT
endmodule

module get_info (
  input  [15:0] IO_IN,
  output [9:0] mantissa,
  output [4:0] exp,
  output sign
);


  assign exp = IO_IN[14:10];
  assign mantissa = IO_IN[9:0];
  assign sign = IO_IN[15];
endmodule

module is_nan (
  input  [9:0] mant,
  input  [4:0] exp,
  output NAN
);

  wire and_1_out, or_1_out;

  and and_1 (and_1_out, exp[0], exp[1], exp[2], exp[3], exp[4]);
  or or_1 (or_1_out, mant[0], mant[1], mant[2], mant[3], mant[4], mant[5], mant[6], mant[7], mant[8], mant[9]);
  and and_2 (NAN, or_1_out, and_1_out);
endmodule

module is_pinf (
  input  [9:0] mant,
  input  [4:0] exp,
  input  sign,
  output PINF
);

  wire and_1_out, or_1_out;

  and and_1 (and_1_out, exp[0], exp[1], exp[2], exp[3], exp[4]);
  or or_1 (or_1_out, mant[0], mant[1], mant[2], mant[3], mant[4], mant[5], mant[6], mant[7], mant[8], mant[9]);
  and and_2 (PINF, ~or_1_out, ~sign, and_1_out);  // AND_Gate
endmodule

module is_ninf (
  input  [9:0] mant,
  input  [4:0] exp,
  input  sign,
  output NINF
);

  wire and_1_out, or_1_out;

  and and_1 (and_1_out, exp[0], exp[1], exp[2], exp[3], exp[4]);
  or or_1 (or_1_out, mant[0], mant[1], mant[2], mant[3], mant[4], mant[5], mant[6], mant[7], mant[8], mant[9]);
  and and_2 (NINF, ~or_1_out, sign, and_1_out);  // AND_Gate
endmodule

module special_cases (
  input  [9:0] mant,
  input  [4:0] exp,
  input  sign,
  output NAN,
  output PINF,
  output NINF,
  output ZERO
);

  wire and_1_out, is_nan_1_nan, is_ninf_1_ninf;

  is_nan is_nan_1 (.mant(mant), .exp(exp), .NAN(is_nan_1_nan));
  is_pinf is_pinf_1 (.mant(mant), .exp(exp), .sign(sign), .PINF(PINF));
  is_ninf is_ninf_1 (.mant(mant), .exp(exp), .sign(sign), .NINF(is_ninf_1_ninf));
  is_zero is_zero_1 (.mant(mant), .exp(exp), .ZERO(ZERO));
  and and_1 (and_1_out, ~is_nan_1_nan, ~PINF, ~is_ninf_1_ninf, ~ZERO, sign);  // AND_Gate
  or or_1 (NAN, is_nan_1_nan, is_ninf_1_ninf, and_1_out);

  assign NINF = 1'b0;
endmodule

module correct_exp_and_mant (
  input  [4:0] exp,
  input  [10:0] mantissa,
  output [23:0] new_exp,
  output [23:0] new_mant
);

  wire comparator_24bit_1_a_bigger_b, comparator_24bit_1_a_equal_b, comparator_24bit_1_a_smaller_b,
       not_1_out, summator_24bit_1_borrow_out, summator_24bit_2_borrow_out, summator_24bit_3_borrow_out,
       undriven, undriven_2, undriven_3, xor_1_out, xor_2_out;
  wire [10:0] correct_mant_1_full_mantissa, correct_mant_2_full_mantissa;
  wire [23:0] correct_mant_1_counter_for_denormal, exp2, exp_t, from_5_24_1_io_in, from_11_24_1_io_in,
       from_11_24_2_io_in, if_expression_4_io_out, mant, mant2, shift_left_1_io_out, shift_left_2_io_out,
       shift_right_1_io_out, shift_right_2_io_out, shift_right_3_io_out, shift_right_4_io_out,
       substructor_24bit_1_out_3, summator_24bit_1_io_out, summator_24bit_2_io_out, summator_24bit_3_io_out;

  from_5_24 from_5_24_1 (.IO_DATA(exp), .IO_IN(from_5_24_1_io_in));
  // NoConnect on undriven
  // NoConnect on comparator_24bit_1_a_smaller_b
  comparator_24bit comparator_24bit_1 (
    .B(from_5_24_1_io_in), .A({24{1'b0}}), .A_smaller_B(comparator_24bit_1_a_smaller_b),
    .A_equal_B(comparator_24bit_1_a_equal_b), .A_bigger_B(comparator_24bit_1_a_bigger_b));
  // NoConnect on comparator_24bit_1_a_bigger_b
  correct_mant correct_mant_1 (
    .exp(exp), .mantissa(mantissa), .full_mantissa(correct_mant_1_full_mantissa),
    .counter_for_denormal(correct_mant_1_counter_for_denormal));
  xor xor_1 (xor_1_out, 1'b0, from_5_24_1_io_in[0]);
  // NoConnect on undriven_2
  from_11_24 from_11_24_1 (.IO_DATA(correct_mant_1_full_mantissa), .IO_IN(from_11_24_1_io_in));
  summator_24bit summator_24bit_1 (
    .A(24'hf), .Borrow_in(undriven), .B(from_5_24_1_io_in), .IO_OUT(summator_24bit_1_io_out),
    .Borrow_out(summator_24bit_1_borrow_out));
  // NoConnect on summator_24bit_1_borrow_out
  xor xor_2 (xor_2_out, 1'b0, correct_mant_1_counter_for_denormal[0]);
  summator_24bit summator_24bit_2 (
    .A(correct_mant_1_counter_for_denormal), .Borrow_in(undriven_2), .B(24'he),
    .IO_OUT(summator_24bit_2_io_out), .Borrow_out(summator_24bit_2_borrow_out));
  // NoConnect on summator_24bit_2_borrow_out
  shift_left shift_left_1 (.IO_IN(from_11_24_1_io_in), .IO_OUT(shift_left_1_io_out));
  // NoConnect on undriven_3
  if_expression if_expression_1 (.A(exp2), .expression(comparator_24bit_1_a_equal_b), .B(exp_t), .IO_OUT(new_exp));
  if_expression if_expression_2 (.A(mant2), .expression(comparator_24bit_1_a_equal_b), .B(mant), .IO_OUT(new_mant));
  shift_right shift_right_1 (.IO_IN(summator_24bit_2_io_out), .IO_OUT(shift_right_1_io_out));
  shift_right shift_right_2 (.IO_IN(summator_24bit_1_io_out), .IO_OUT(shift_right_2_io_out));
  substructor_24bit substructor_24bit_1 (
    .subtrahend(24'h1), .minuend(summator_24bit_1_io_out), .out_3(substructor_24bit_1_out_3));
  if_expression if_expression_3 (
    .A(shift_left_1_io_out), .expression(xor_2_out), .B(from_11_24_1_io_in), .IO_OUT(mant2));
  summator_24bit summator_24bit_3 (
    .A(summator_24bit_2_io_out), .Borrow_in(undriven_3), .B(24'h1), .IO_OUT(summator_24bit_3_io_out),
    .Borrow_out(summator_24bit_3_borrow_out));
  // NoConnect on summator_24bit_3_borrow_out
  shift_right shift_right_3 (.IO_IN(substructor_24bit_1_out_3), .IO_OUT(shift_right_3_io_out));
  shift_right shift_right_4 (.IO_IN(summator_24bit_3_io_out), .IO_OUT(shift_right_4_io_out));
  not not_1 (not_1_out, xor_1_out);
  correct_mant correct_mant_2 (
    .exp(exp), .mantissa(mantissa), .full_mantissa(correct_mant_2_full_mantissa));  // open: counter_for_denormal
  if_expression if_expression_4 (
    .A(shift_right_4_io_out), .expression(xor_2_out), .B(shift_right_1_io_out),
    .IO_OUT(if_expression_4_io_out));
  if_expression if_expression_5 (
    .A(shift_right_2_io_out), .expression(xor_1_out), .B(shift_right_3_io_out), .IO_OUT(exp_t));
  shift_left shift_left_2 (.IO_IN(from_11_24_2_io_in), .IO_OUT(shift_left_2_io_out));
  from_11_24 from_11_24_2 (.IO_DATA(correct_mant_2_full_mantissa), .IO_IN(from_11_24_2_io_in));
  substructor_24bit substructor_24bit_2 (.subtrahend(if_expression_4_io_out), .minuend(24'hf), .out_3(exp2));
  if_expression if_expression_6 (
    .A(shift_left_2_io_out), .expression(not_1_out), .B(from_11_24_2_io_in), .IO_OUT(mant));
endmodule

module correct_mant (
  input  [4:0] exp,
  input  [10:0] mantissa,
  output [10:0] full_mantissa,
  output [23:0] counter_for_denormal
);

  wire is_first_bit_one_1_first_bit_zero, is_first_bit_one_2_first_bit_zero,
       is_first_bit_one_3_first_bit_zero, is_first_bit_one_4_first_bit_zero,
       is_first_bit_one_5_first_bit_zero, is_first_bit_one_6_first_bit_zero,
       is_first_bit_one_7_first_bit_zero, is_first_bit_one_8_first_bit_zero,
       is_first_bit_one_9_first_bit_zero, is_first_bit_one_10_first_bit_zero, or_1_out,
       summator_24bit_1_borrow_out, undriven;
  wire [23:0] from_11_24_1_io_in, if_expression_1_io_out, if_expression_2_io_out, if_expression_3_io_out,
       if_expression_4_io_out, if_expression_5_io_out, if_expression_6_io_out, if_expression_7_io_out,
       if_expression_8_io_out, if_expression_9_io_out, if_expression_10_io_out, if_expression_11_io_out,
       if_expression_13_io_out, if_expression_14_io_out, if_expression_15_io_out, if_expression_16_io_out,
       if_expression_17_io_out, if_expression_18_io_out, if_expression_19_io_out, if_expression_20_io_out,
       if_expression_21_io_out, shift_left_1_io_out, shift_left_2_io_out, shift_left_3_io_out,
       shift_left_4_io_out, shift_left_5_io_out, shift_left_6_io_out, shift_left_7_io_out,
       shift_left_8_io_out, shift_left_9_io_out, shift_left_10_io_out, summator_24bit_1_io_out;

  from_11_24 from_11_24_1 (.IO_DATA(mantissa), .IO_IN(from_11_24_1_io_in));
  // NoConnect on undriven
  or or_1 (or_1_out, exp[0], exp[1], exp[2], exp[3], exp[4]);
  summator_24bit summator_24bit_1 (
    .A(24'h400), .Borrow_in(undriven), .B(from_11_24_1_io_in), .IO_OUT(summator_24bit_1_io_out),
    .Borrow_out(summator_24bit_1_borrow_out));
  // NoConnect on summator_24bit_1_borrow_out
  shift_left shift_left_1 (.IO_IN(from_11_24_1_io_in), .IO_OUT(shift_left_1_io_out));
  shift_left shift_left_2 (.IO_IN(shift_left_1_io_out), .IO_OUT(shift_left_2_io_out));
  shift_left shift_left_3 (.IO_IN(shift_left_2_io_out), .IO_OUT(shift_left_3_io_out));
  shift_left shift_left_4 (.IO_IN(shift_left_3_io_out), .IO_OUT(shift_left_4_io_out));
  shift_left shift_left_5 (.IO_IN(shift_left_4_io_out), .IO_OUT(shift_left_5_io_out));
  shift_left shift_left_6 (.IO_IN(shift_left_5_io_out), .IO_OUT(shift_left_6_io_out));
  shift_left shift_left_7 (.IO_IN(shift_left_6_io_out), .IO_OUT(shift_left_7_io_out));
  shift_left shift_left_8 (.IO_IN(shift_left_7_io_out), .IO_OUT(shift_left_8_io_out));
  shift_left shift_left_9 (.IO_IN(shift_left_8_io_out), .IO_OUT(shift_left_9_io_out));
  shift_left shift_left_10 (.IO_IN(shift_left_9_io_out), .IO_OUT(shift_left_10_io_out));
  is_first_bit_one is_first_bit_one_1 (.in_1(shift_left_1_io_out), .first_bit_zero(is_first_bit_one_1_first_bit_zero));
  is_first_bit_one is_first_bit_one_2 (.in_1(shift_left_2_io_out), .first_bit_zero(is_first_bit_one_2_first_bit_zero));
  is_first_bit_one is_first_bit_one_3 (.in_1(shift_left_3_io_out), .first_bit_zero(is_first_bit_one_3_first_bit_zero));
  is_first_bit_one is_first_bit_one_4 (.in_1(shift_left_4_io_out), .first_bit_zero(is_first_bit_one_4_first_bit_zero));
  is_first_bit_one is_first_bit_one_5 (.in_1(shift_left_5_io_out), .first_bit_zero(is_first_bit_one_5_first_bit_zero));
  is_first_bit_one is_first_bit_one_6 (.in_1(shift_left_6_io_out), .first_bit_zero(is_first_bit_one_6_first_bit_zero));
  is_first_bit_one is_first_bit_one_7 (.in_1(shift_left_7_io_out), .first_bit_zero(is_first_bit_one_7_first_bit_zero));
  is_first_bit_one is_first_bit_one_8 (.in_1(shift_left_8_io_out), .first_bit_zero(is_first_bit_one_8_first_bit_zero));
  is_first_bit_one is_first_bit_one_9 (.in_1(shift_left_9_io_out), .first_bit_zero(is_first_bit_one_9_first_bit_zero));
  is_first_bit_one is_first_bit_one_10 (
    .in_1(shift_left_10_io_out), .first_bit_zero(is_first_bit_one_10_first_bit_zero));
  if_expression if_expression_1 (
    .A(summator_24bit_1_io_out), .expression(or_1_out), .B(if_expression_2_io_out),
    .IO_OUT(if_expression_1_io_out));
  if_expression if_expression_2 (
    .A(shift_left_1_io_out), .expression(is_first_bit_one_1_first_bit_zero), .B(if_expression_3_io_out),
    .IO_OUT(if_expression_2_io_out));
  if_expression if_expression_3 (
    .A(shift_left_2_io_out), .expression(is_first_bit_one_2_first_bit_zero), .B(if_expression_4_io_out),
    .IO_OUT(if_expression_3_io_out));
  if_expression if_expression_4 (
    .A(shift_left_3_io_out), .expression(is_first_bit_one_3_first_bit_zero), .B(if_expression_5_io_out),
    .IO_OUT(if_expression_4_io_out));
  if_expression if_expression_5 (
    .A(shift_left_4_io_out), .expression(is_first_bit_one_4_first_bit_zero), .B(if_expression_6_io_out),
    .IO_OUT(if_expression_5_io_out));
  if_expression if_expression_6 (
    .A(shift_left_5_io_out), .expression(is_first_bit_one_5_first_bit_zero), .B(if_expression_7_io_out),
    .IO_OUT(if_expression_6_io_out));
  if_expression if_expression_7 (
    .A(shift_left_6_io_out), .expression(is_first_bit_one_6_first_bit_zero), .B(if_expression_8_io_out),
    .IO_OUT(if_expression_7_io_out));
  if_expression if_expression_8 (
    .A(shift_left_7_io_out), .expression(is_first_bit_one_7_first_bit_zero), .B(if_expression_9_io_out),
    .IO_OUT(if_expression_8_io_out));
  if_expression if_expression_9 (
    .A(shift_left_8_io_out), .expression(is_first_bit_one_8_first_bit_zero), .B(if_expression_10_io_out),
    .IO_OUT(if_expression_9_io_out));
  if_expression if_expression_10 (
    .A(shift_left_9_io_out), .expression(is_first_bit_one_9_first_bit_zero), .B(if_expression_11_io_out),
    .IO_OUT(if_expression_10_io_out));
  if_expression if_expression_11 (
    .A(shift_left_10_io_out), .expression(is_first_bit_one_10_first_bit_zero), .B({24{1'b0}}),
    .IO_OUT(if_expression_11_io_out));
  from_24_11 from_24_11_1 (.IO_IN(if_expression_1_io_out), .IO_DATA(full_mantissa));
  if_expression if_expression_12 (
    .A(24'h1), .expression(is_first_bit_one_1_first_bit_zero), .B(if_expression_13_io_out),
    .IO_OUT(counter_for_denormal));
  if_expression if_expression_13 (
    .A(24'h2), .expression(is_first_bit_one_2_first_bit_zero), .B(if_expression_14_io_out),
    .IO_OUT(if_expression_13_io_out));
  if_expression if_expression_14 (
    .A(24'h3), .expression(is_first_bit_one_3_first_bit_zero), .B(if_expression_15_io_out),
    .IO_OUT(if_expression_14_io_out));
  if_expression if_expression_15 (
    .A(24'h4), .expression(is_first_bit_one_4_first_bit_zero), .B(if_expression_16_io_out),
    .IO_OUT(if_expression_15_io_out));
  if_expression if_expression_16 (
    .A(24'h5), .expression(is_first_bit_one_5_first_bit_zero), .B(if_expression_17_io_out),
    .IO_OUT(if_expression_16_io_out));
  if_expression if_expression_17 (
    .A(24'h6), .expression(is_first_bit_one_6_first_bit_zero), .B(if_expression_18_io_out),
    .IO_OUT(if_expression_17_io_out));
  if_expression if_expression_18 (
    .A(24'h7), .expression(is_first_bit_one_7_first_bit_zero), .B(if_expression_19_io_out),
    .IO_OUT(if_expression_18_io_out));
  if_expression if_expression_19 (
    .A(24'h8), .expression(is_first_bit_one_8_first_bit_zero), .B(if_expression_20_io_out),
    .IO_OUT(if_expression_19_io_out));
  if_expression if_expression_20 (
    .A(24'h9), .expression(is_first_bit_one_9_first_bit_zero), .B(if_expression_21_io_out),
    .IO_OUT(if_expression_20_io_out));
  if_expression if_expression_21 (
    .A(24'ha), .expression(is_first_bit_one_10_first_bit_zero), .B({24{1'b0}}),
    .IO_OUT(if_expression_21_io_out));
endmodule

module shift_right (
  input  [23:0] IO_IN,
  output [23:0] IO_OUT
);

  // NoConnect on IO_IN[0]

  assign IO_OUT = {1'b0, IO_IN[23:1]};
endmodule

module counter_4bit (
  input  C,
  input  ENABLE,
  output [3:0] out_3
);

  wire jk_trigger_1_nq, jk_trigger_1_q, jk_trigger_2_nq, jk_trigger_2_q, jk_trigger_3_nq, jk_trigger_3_q,
       jk_trigger_4_nq, not_1_out;

  not not_1 (not_1_out, ENABLE);
  jk_trigger jk_trigger_1 (.J(C), .C(C), .K(C), .ENABLE(not_1_out), .Q(jk_trigger_1_q), .NQ(jk_trigger_1_nq));
  jk_trigger jk_trigger_2 (
    .J(C), .C(jk_trigger_1_q), .K(C), .ENABLE(not_1_out), .Q(jk_trigger_2_q), .NQ(jk_trigger_2_nq));
  not not_2 (out_3[1], jk_trigger_2_nq);
  jk_trigger jk_trigger_3 (
    .J(C), .C(jk_trigger_2_q), .K(C), .ENABLE(not_1_out), .Q(jk_trigger_3_q), .NQ(jk_trigger_3_nq));
  not not_3 (out_3[2], jk_trigger_3_nq);
  jk_trigger jk_trigger_4 (.J(C), .C(jk_trigger_3_q), .K(C), .ENABLE(not_1_out), .NQ(jk_trigger_4_nq));  // open: Q
  not not_4 (out_3[3], jk_trigger_4_nq);
  not not_5 (out_3[0], jk_trigger_1_nq);
endmodule

module jk_trigger (
  input  J,
  input  C,
  input  K,
  input  ENABLE,
  output Q,
  output NQ
);

  wire and_1_out, and_2_out, not_1_out, synch_rs_trigger_1_nq, synch_rs_trigger_1_q;

  and and_1 (and_1_out, Q, J);
  and and_2 (and_2_out, K, NQ);
  not not_1 (not_1_out, C);
  synch_rs_trigger synch_rs_trigger_1 (
    .R(and_1_out), .C(C), .S(and_2_out), .ENABLE(ENABLE), .Q(synch_rs_trigger_1_q), .NQ(synch_rs_trigger_1_nq));
  synch_rs_trigger synch_rs_trigger_2 (
    .R(synch_rs_trigger_1_nq), .C(not_1_out), .S(synch_rs_trigger_1_q), .ENABLE(ENABLE), .Q(Q), .NQ(NQ));
endmodule

module is_zero (
  input  [9:0] mant,
  input  [4:0] exp,
  output ZERO
);

  wire or_1_out, or_2_out;

  or or_1 (or_1_out, exp[0], exp[1], exp[2], exp[3], exp[4]);
  or or_2 (or_2_out, mant[0], mant[1], mant[2], mant[3], mant[4], mant[5], mant[6], mant[7], mant[8], mant[9]);
  and and_1 (ZERO, ~or_2_out, ~or_1_out);  // AND_Gate
endmodule

module substructor_16bit (
  input  [15:0] minuend,
  input  [15:0] subtrahend,
  input  borrow_in,
  output [15:0] difference,
  output borrow_out
);

  wire substructor_1_borrow_out, substructor_2_borrow_out, substructor_3_borrow_out,
       substructor_4_borrow_out, substructor_5_borrow_out, substructor_6_borrow_out,
       substructor_7_borrow_out, substructor_8_borrow_out, substructor_9_borrow_out,
       substructor_10_borrow_out, substructor_11_borrow_out, substructor_12_borrow_out,
       substructor_13_borrow_out, substructor_14_borrow_out, substructor_15_borrow_out;

  substructor substructor_1 (
    .borrow_in(borrow_in), .minuend(minuend[0]), .subtrahend(subtrahend[0]), .difference(difference[0]),
    .borrow_out(substructor_1_borrow_out));
  substructor substructor_2 (
    .borrow_in(substructor_1_borrow_out), .minuend(minuend[1]), .subtrahend(subtrahend[1]),
    .difference(difference[1]), .borrow_out(substructor_2_borrow_out));
  substructor substructor_3 (
    .borrow_in(substructor_2_borrow_out), .minuend(minuend[2]), .subtrahend(subtrahend[2]),
    .difference(difference[2]), .borrow_out(substructor_3_borrow_out));
  substructor substructor_4 (
    .borrow_in(substructor_3_borrow_out), .minuend(minuend[3]), .subtrahend(subtrahend[3]),
    .difference(difference[3]), .borrow_out(substructor_4_borrow_out));
  substructor substructor_5 (
    .borrow_in(substructor_4_borrow_out), .minuend(minuend[4]), .subtrahend(subtrahend[4]),
    .difference(difference[4]), .borrow_out(substructor_5_borrow_out));
  substructor substructor_6 (
    .borrow_in(substructor_5_borrow_out), .minuend(minuend[5]), .subtrahend(subtrahend[5]),
    .difference(difference[5]), .borrow_out(substructor_6_borrow_out));
  substructor substructor_7 (
    .borrow_in(substructor_6_borrow_out), .minuend(minuend[6]), .subtrahend(subtrahend[6]),
    .difference(difference[6]), .borrow_out(substructor_7_borrow_out));
  substructor substructor_8 (
    .borrow_in(substructor_7_borrow_out), .minuend(minuend[7]), .subtrahend(subtrahend[7]),
    .difference(difference[7]), .borrow_out(substructor_8_borrow_out));
  substructor substructor_9 (
    .borrow_in(substructor_8_borrow_out), .minuend(minuend[8]), .subtrahend(subtrahend[8]),
    .difference(difference[8]), .borrow_out(substructor_9_borrow_out));
  substructor substructor_10 (
    .borrow_in(substructor_9_borrow_out), .minuend(minuend[9]), .subtrahend(subtrahend[9]),
    .difference(difference[9]), .borrow_out(substructor_10_borrow_out));
  substructor substructor_11 (
    .borrow_in(substructor_10_borrow_out), .minuend(minuend[10]), .subtrahend(subtrahend[10]),
    .difference(difference[10]), .borrow_out(substructor_11_borrow_out));
  substructor substructor_12 (
    .borrow_in(substructor_11_borrow_out), .minuend(minuend[11]), .subtrahend(subtrahend[11]),
    .difference(difference[11]), .borrow_out(substructor_12_borrow_out));
  substructor substructor_13 (
    .borrow_in(substructor_12_borrow_out), .minuend(minuend[12]), .subtrahend(subtrahend[12]),
    .difference(difference[12]), .borrow_out(substructor_13_borrow_out));
  substructor substructor_14 (
    .borrow_in(substructor_13_borrow_out), .minuend(minuend[13]), .subtrahend(subtrahend[13]),
    .difference(difference[13]), .borrow_out(substructor_14_borrow_out));
  substructor substructor_15 (
    .borrow_in(substructor_14_borrow_out), .minuend(minuend[14]), .subtrahend(subtrahend[14]),
    .difference(difference[14]), .borrow_out(substructor_15_borrow_out));
  substructor substructor_16 (
    .borrow_in(substructor_15_borrow_out), .minuend(minuend[15]), .subtrahend(subtrahend[15]),
    .difference(difference[15]), .borrow_out(borrow_out));
endmodule

module comparator_16bit (
  input  [15:0] B,
  input  [15:0] A,
  input  oldA_smaller_B,
  input  oldA_equal_B,
  input  oldA_bigger_B,
  output A_smaller_B,
  output A_equal_B,
  output A_bigger_B
);

  wire comparator_1bit_2_a_bigger_b, comparator_1bit_2_a_equal_b, comparator_1bit_2_a_smaller_b,
       comparator_1bit_3_a_bigger_b, comparator_1bit_3_a_equal_b, comparator_1bit_3_a_smaller_b,
       comparator_1bit_4_a_bigger_b, comparator_1bit_4_a_equal_b, comparator_1bit_4_a_smaller_b,
       comparator_1bit_5_a_bigger_b, comparator_1bit_5_a_equal_b, comparator_1bit_5_a_smaller_b,
       comparator_1bit_6_a_bigger_b, comparator_1bit_6_a_equal_b, comparator_1bit_6_a_smaller_b,
       comparator_1bit_7_a_bigger_b, comparator_1bit_7_a_equal_b, comparator_1bit_7_a_smaller_b,
       comparator_1bit_8_a_bigger_b, comparator_1bit_8_a_equal_b, comparator_1bit_8_a_smaller_b,
       comparator_1bit_9_a_bigger_b, comparator_1bit_9_a_equal_b, comparator_1bit_9_a_smaller_b,
       comparator_1bit_10_a_bigger_b, comparator_1bit_10_a_equal_b, comparator_1bit_10_a_smaller_b,
       comparator_1bit_11_a_bigger_b, comparator_1bit_11_a_equal_b, comparator_1bit_11_a_smaller_b,
       comparator_1bit_12_a_bigger_b, comparator_1bit_12_a_equal_b, comparator_1bit_12_a_smaller_b,
       comparator_1bit_13_a_bigger_b, comparator_1bit_13_a_equal_b, comparator_1bit_13_a_smaller_b,
       comparator_1bit_14_a_bigger_b, comparator_1bit_14_a_equal_b, comparator_1bit_14_a_smaller_b,
       comparator_1bit_15_a_bigger_b, comparator_1bit_15_a_equal_b, comparator_1bit_15_a_smaller_b,
       comparator_1bit_16_a_bigger_b, comparator_1bit_16_a_equal_b, comparator_1bit_16_a_smaller_b;

  comparator_1bit comparator_1bit_1 (
    .A(A[15]), .B(B[15]), .oldA_smaller_oldB(comparator_1bit_2_a_smaller_b),
    .oldA_equal_oldB(comparator_1bit_2_a_equal_b), .oldA_bigger_oldB(comparator_1bit_2_a_bigger_b),
    .A_smaller_B(A_smaller_B), .A_equal_B(A_equal_B), .A_bigger_B(A_bigger_B));
  comparator_1bit comparator_1bit_2 (
    .A(A[14]), .B(B[14]), .oldA_smaller_oldB(comparator_1bit_3_a_smaller_b),
    .oldA_equal_oldB(comparator_1bit_3_a_equal_b), .oldA_bigger_oldB(comparator_1bit_3_a_bigger_b),
    .A_smaller_B(comparator_1bit_2_a_smaller_b), .A_equal_B(comparator_1bit_2_a_equal_b),
    .A_bigger_B(comparator_1bit_2_a_bigger_b));
  comparator_1bit comparator_1bit_3 (
    .A(A[13]), .B(B[13]), .oldA_smaller_oldB(comparator_1bit_4_a_smaller_b),
    .oldA_equal_oldB(comparator_1bit_4_a_equal_b), .oldA_bigger_oldB(comparator_1bit_4_a_bigger_b),
    .A_smaller_B(comparator_1bit_3_a_smaller_b), .A_equal_B(comparator_1bit_3_a_equal_b),
    .A_bigger_B(comparator_1bit_3_a_bigger_b));
  comparator_1bit comparator_1bit_4 (
    .A(A[12]), .B(B[12]), .oldA_smaller_oldB(comparator_1bit_5_a_smaller_b),
    .oldA_equal_oldB(comparator_1bit_5_a_equal_b), .oldA_bigger_oldB(comparator_1bit_5_a_bigger_b),
    .A_smaller_B(comparator_1bit_4_a_smaller_b), .A_equal_B(comparator_1bit_4_a_equal_b),
    .A_bigger_B(comparator_1bit_4_a_bigger_b));
  comparator_1bit comparator_1bit_5 (
    .A(A[11]), .B(B[11]), .oldA_smaller_oldB(comparator_1bit_6_a_smaller_b),
    .oldA_equal_oldB(comparator_1bit_6_a_equal_b), .oldA_bigger_oldB(comparator_1bit_6_a_bigger_b),
    .A_smaller_B(comparator_1bit_5_a_smaller_b), .A_equal_B(comparator_1bit_5_a_equal_b),
    .A_bigger_B(comparator_1bit_5_a_bigger_b));
  comparator_1bit comparator_1bit_6 (
    .A(A[10]), .B(B[10]), .oldA_smaller_oldB(comparator_1bit_7_a_smaller_b),
    .oldA_equal_oldB(comparator_1bit_7_a_equal_b), .oldA_bigger_oldB(comparator_1bit_7_a_bigger_b),
    .A_smaller_B(comparator_1bit_6_a_smaller_b), .A_equal_B(comparator_1bit_6_a_equal_b),
    .A_bigger_B(comparator_1bit_6_a_bigger_b));
  comparator_1bit comparator_1bit_7 (
    .A(A[9]), .B(B[9]), .oldA_smaller_oldB(comparator_1bit_8_a_smaller_b),
    .oldA_equal_oldB(comparator_1bit_8_a_equal_b), .oldA_bigger_oldB(comparator_1bit_8_a_bigger_b),
    .A_smaller_B(comparator_1bit_7_a_smaller_b), .A_equal_B(comparator_1bit_7_a_equal_b),
    .A_bigger_B(comparator_1bit_7_a_bigger_b));
  comparator_1bit comparator_1bit_8 (
    .A(A[8]), .B(B[8]), .oldA_smaller_oldB(comparator_1bit_9_a_smaller_b),
    .oldA_equal_oldB(comparator_1bit_9_a_equal_b), .oldA_bigger_oldB(comparator_1bit_9_a_bigger_b),
    .A_smaller_B(comparator_1bit_8_a_smaller_b), .A_equal_B(comparator_1bit_8_a_equal_b),
    .A_bigger_B(comparator_1bit_8_a_bigger_b));
  comparator_1bit comparator_1bit_9 (
    .A(A[7]), .B(B[7]), .oldA_smaller_oldB(comparator_1bit_10_a_smaller_b),
    .oldA_equal_oldB(comparator_1bit_10_a_equal_b), .oldA_bigger_oldB(comparator_1bit_10_a_bigger_b),
    .A_smaller_B(comparator_1bit_9_a_smaller_b), .A_equal_B(comparator_1bit_9_a_equal_b),
    .A_bigger_B(comparator_1bit_9_a_bigger_b));
  comparator_1bit comparator_1bit_10 (
    .A(A[6]), .B(B[6]), .oldA_smaller_oldB(comparator_1bit_11_a_smaller_b),
    .oldA_equal_oldB(comparator_1bit_11_a_equal_b), .oldA_bigger_oldB(comparator_1bit_11_a_bigger_b),
    .A_smaller_B(comparator_1bit_10_a_smaller_b), .A_equal_B(comparator_1bit_10_a_equal_b),
    .A_bigger_B(comparator_1bit_10_a_bigger_b));
  comparator_1bit comparator_1bit_11 (
    .A(A[5]), .B(B[5]), .oldA_smaller_oldB(comparator_1bit_12_a_smaller_b),
    .oldA_equal_oldB(comparator_1bit_12_a_equal_b), .oldA_bigger_oldB(comparator_1bit_12_a_bigger_b),
    .A_smaller_B(comparator_1bit_11_a_smaller_b), .A_equal_B(comparator_1bit_11_a_equal_b),
    .A_bigger_B(comparator_1bit_11_a_bigger_b));
  comparator_1bit comparator_1bit_12 (
    .A(A[4]), .B(B[4]), .oldA_smaller_oldB(comparator_1bit_13_a_smaller_b),
    .oldA_equal_oldB(comparator_1bit_13_a_equal_b), .oldA_bigger_oldB(comparator_1bit_13_a_bigger_b),
    .A_smaller_B(comparator_1bit_12_a_smaller_b), .A_equal_B(comparator_1bit_12_a_equal_b),
    .A_bigger_B(comparator_1bit_12_a_bigger_b));
  comparator_1bit comparator_1bit_13 (
    .A(A[3]), .B(B[3]), .oldA_smaller_oldB(comparator_1bit_14_a_smaller_b),
    .oldA_equal_oldB(comparator_1bit_14_a_equal_b), .oldA_bigger_oldB(comparator_1bit_14_a_bigger_b),
    .A_smaller_B(comparator_1bit_13_a_smaller_b), .A_equal_B(comparator_1bit_13_a_equal_b),
    .A_bigger_B(comparator_1bit_13_a_bigger_b));
  comparator_1bit comparator_1bit_14 (
    .A(A[2]), .B(B[2]), .oldA_smaller_oldB(comparator_1bit_15_a_smaller_b),
    .oldA_equal_oldB(comparator_1bit_15_a_equal_b), .oldA_bigger_oldB(comparator_1bit_15_a_bigger_b),
    .A_smaller_B(comparator_1bit_14_a_smaller_b), .A_equal_B(comparator_1bit_14_a_equal_b),
    .A_bigger_B(comparator_1bit_14_a_bigger_b));
  comparator_1bit comparator_1bit_15 (
    .A(A[1]), .B(B[1]), .oldA_smaller_oldB(comparator_1bit_16_a_smaller_b),
    .oldA_equal_oldB(comparator_1bit_16_a_equal_b), .oldA_bigger_oldB(comparator_1bit_16_a_bigger_b),
    .A_smaller_B(comparator_1bit_15_a_smaller_b), .A_equal_B(comparator_1bit_15_a_equal_b),
    .A_bigger_B(comparator_1bit_15_a_bigger_b));
  comparator_1bit comparator_1bit_16 (
    .A(A[0]), .B(B[0]), .oldA_smaller_oldB(oldA_smaller_B), .oldA_equal_oldB(oldA_equal_B),
    .oldA_bigger_oldB(oldA_bigger_B), .A_smaller_B(comparator_1bit_16_a_smaller_b),
    .A_equal_B(comparator_1bit_16_a_equal_b), .A_bigger_B(comparator_1bit_16_a_bigger_b));
endmodule

module is_first_bit_one (
  input  [23:0] in_1,
  output first_bit_zero
);

  comparator_1bit comparator_1bit_1 (
    .A(1'b1), .B(in_1[10]), .oldA_smaller_oldB(1'b0), .oldA_equal_oldB(1'b1), .oldA_bigger_oldB(1'b0),
    .A_equal_B(first_bit_zero));  // open: A_smaller_B, A_bigger_B
endmodule

module get_res (
  input  [23:0] mant,
  input  [23:0] exp,
  input  [23:0] sign,
  output [15:0] res
);


  assign res = {sign[0], exp[4:0], mant[9:0]};
endmodule

module output_special_cases (
  input  [9:0] mant,
  input  [4:0] exp,
  input  sign,
  output [23:0] IO_OUT
);

  wire and_1_out, and_2_out, is_nan_1_nan, is_ninf_1_ninf, is_pinf_1_pinf, is_zero_1_zero, or_1_out;
  wire [23:0] from_16_24_1_io_data, if_expression_1_io_out, if_expression_2_io_out, if_expression_3_io_out,
       if_expression_4_io_out, if_expression_5_io_out, make_qnan_1_io_data;

  is_nan is_nan_1 (.mant(mant), .exp(exp), .NAN(is_nan_1_nan));
  is_pinf is_pinf_1 (.mant(mant), .exp(exp), .sign(sign), .PINF(is_pinf_1_pinf));
  is_ninf is_ninf_1 (.mant(mant), .exp(exp), .sign(sign), .NINF(is_ninf_1_ninf));
  is_zero is_zero_1 (.mant(mant), .exp(exp), .ZERO(is_zero_1_zero));
  from_16_24 from_16_24_1 (.IO_IN({sign, exp, mant}), .IO_DATA(from_16_24_1_io_data));
  and and_1 (and_1_out, ~is_zero_1_zero, sign);  // AND_Gate
  or or_1 (or_1_out, is_ninf_1_ninf, and_1_out);
  make_qnan make_qnan_1 (.IO_IN(from_16_24_1_io_data), .IO_DATA(make_qnan_1_io_data));
  and and_2 (and_2_out, is_zero_1_zero, sign);
  if_expression if_expression_1 (
    .A(make_qnan_1_io_data), .expression(is_nan_1_nan), .IO_OUT(if_expression_1_io_out));  // open: B
  if_expression if_expression_2 (
    .A(24'h7c00), .expression(is_pinf_1_pinf), .IO_OUT(if_expression_2_io_out));  // open: B
  if_expression if_expression_3 (.A(24'hfe00), .expression(or_1_out), .IO_OUT(if_expression_3_io_out));  // open: B
  if_expression if_expression_4 (
    .A({24{1'b0}}), .expression(is_zero_1_zero), .IO_OUT(if_expression_4_io_out));  // open: B
  if_expression if_expression_5 (.A(24'h8000), .expression(and_2_out), .IO_OUT(if_expression_5_io_out));  // open: B
  assign IO_OUT = if_expression_1_io_out | if_expression_2_io_out | if_expression_3_io_out | if_expression_4_io_out | if_expression_5_io_out;  // OR_Gate or_2, 24 bits wide
endmodule

module from_16_24 (
  input  [15:0] IO_IN,
  output [23:0] IO_DATA
);


  assign IO_DATA = {{8{1'b0}}, IO_IN};
endmodule

module from_24_11 (
  input  [23:0] IO_IN,
  output [10:0] IO_DATA
);


  assign IO_DATA = IO_IN[10:0];
endmodule

module from_11_24 (
  input  [10:0] IO_DATA,
  output [23:0] IO_IN
);


  assign IO_IN = {{13{1'b0}}, IO_DATA};
endmodule

module from_5_24 (
  input  [4:0] IO_DATA,
  output [23:0] IO_IN
);


  assign IO_IN = {{19{1'b0}}, IO_DATA};
endmodule

module from_24_5 (
  input  [23:0] IO_IN,
  output [4:0] IO_DATA
);


  assign IO_DATA = IO_IN[4:0];
endmodule

module from_2_24 (
  input  [1:0] IO_IN,
  output [23:0] IO_OUT
);


  assign IO_OUT[1:0] = IO_IN;
endmodule

module from_24_16 (
  input  [23:0] IO_DATA,
  output [15:0] IO_IN
);


  assign IO_IN = IO_DATA[15:0];
endmodule

module from_24_10 (
  input  [23:0] IO_IN,
  output [9:0] IO_DATA
);


  assign IO_DATA = IO_IN[9:0];
endmodule

module from_10_11 (
  input  [9:0] IO_IN,
  output [10:0] IO_DATA
);


  assign IO_DATA = {1'b0, IO_IN};
endmodule

module from_10_24 (
  input  [9:0] IO_DATA,
  output [23:0] IO_IN
);


  assign IO_IN = {{14{1'b0}}, IO_DATA};
endmodule

module from_24_1 (
  input  [23:0] IO_IN,
  output IO_DATA
);


  assign IO_DATA = IO_IN[0];
endmodule

module from_1_24 (
  input  IO_IN,
  output [23:0] out_2
);


  assign out_2 = {{23{1'b0}}, IO_IN};
endmodule

module from_4_24 (
  input  [3:0] IO_DATA,
  output [23:0] IO_IN
);


  assign IO_IN = {{20{1'b0}}, IO_DATA};
endmodule

module make_qnan (
  input  [23:0] IO_IN,
  output [23:0] IO_DATA
);


  assign IO_DATA = {IO_IN[23:10], 1'b1, IO_IN[8:0]};
endmodule
